# Fritzing sketch MHW_BG_Box (saved by Fritzing 1.0.2b)
circuit board: 8.46667cm x 5.64444cm

parts:
  Pi_Pico = Raspberry Pi Pico
  S1 = Pushbutton [package="[THT]"]
  S2 = Pushbutton [package="[THT]"]
  S3 = Pushbutton [package="[THT]"]
  S4 = Pushbutton [package="[THT]"]
  S5 = Pushbutton [package="[THT]"]
  SMALL_LED_STRIP = SMD RGB LED (WS2812) [package=5050]
  S6 = Pushbutton [package="[THT]"]
  S7 = Pushbutton [package="[THT]"]
  S8 = Pushbutton [package="[THT]"]
  S9 = Pushbutton [package="[THT]"]
  S10 = Pushbutton [package="[THT]"]
  LARGE_LED_STRIP = SMD RGB LED (WS2812) [package=5050]
  7-SEG = mystery part, 5 pins [chip_label=?]
  U1 = POT [knob_status=50% power=0.5W package=pot_mammoth]
  U2 = POT [knob_status=50% power=0.5W package=pot_mammoth]

nets:
  N1: Pi_Pico.pin_4, 7-SEG.pin4
  N2: Pi_Pico.pin_5, 7-SEG.pin3
  N3: Pi_Pico.pin_7, 7-SEG.pin2
  VDD: Pi_Pico.pin_8, Pi_Pico.pin_23, Pi_Pico.pin_33, Pi_Pico.pin_42, SMALL_LED_STRIP.VDD, LARGE_LED_STRIP.VDD, 7-SEG.pin1, U1.E, U2.E
  N4: Pi_Pico.pin_9, S6.Pin_2
  N5: Pi_Pico.pin_10, S8.Pin_1, S8.Pin_2
  N6: Pi_Pico.pin_11, S7.Pin_1, S7.Pin_2
  N7: Pi_Pico.pin_12, S9.Pin_2
  N8: Pi_Pico.pin_14, S10.Pin_2
  N9: Pi_Pico.pin_15, S5.Pin_2
  N10: Pi_Pico.pin_16, S3.Pin_2
  N11: Pi_Pico.pin_17, S4.Pin_2
  N12: Pi_Pico.pin_19, S2.Pin_2
  N13: Pi_Pico.pin_20, S1.Pin_2
  N14: Pi_Pico.pin_21, LARGE_LED_STRIP.DIn
  N15: Pi_Pico.pin_22, SMALL_LED_STRIP.DIn
  N16: Pi_Pico.pin_31, U1.A
  N17: Pi_Pico.pin_32, U2.A
  N18: Pi_Pico.pin_35, U1.S, U2.S
  N19: Pi_Pico.pin_36, S1.Pin_3, S1.Pin_4, S2.Pin_3, S2.Pin_4, S3.Pin_3, S3.Pin_4, S4.Pin_3, S4.Pin_4, S5.Pin_3, S5.Pin_4, S6.Pin_3, S6.Pin_4, S7.Pin_3, S7.Pin_4, S8.Pin_3, S8.Pin_4, S9.Pin_3, S9.Pin_4, S10.Pin_3, S10.Pin_4
  VCC: Pi_Pico.pin_40, SMALL_LED_STRIP.VCC, LARGE_LED_STRIP.VCC, 7-SEG.pin5

custom parts:
  Raspberry Pi Pico: Raspberry Pi Pico. Based around the RP2040 microcontroller the Pico is a low cost microcontroller device bringing Raspberry Pi quality, cost, and easy of use to the microcontroller space. Jan 2021, Split part in to two versions: tht (this one) and SMD. This one will drill holes for a .1 in header in pcb to allow plugging in the module as well as providing pads to solder the module to the top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
